// Logisim project trafic-light-controller.circ as structural Verilog: 1 circuit, main circuit main
module main (
);

  wire and_1_out, and_2_out, and_3_out, and_4_out, and_5_out, and_6_out, clock_1_out, d_ff_1_q, d_ff_2_q,
       d_ff_3_q, not_1_out, not_2_out, not_3_out, or_1_out, or_2_out, or_3_out, or_4_out, or_5_out;

  not not_1 (not_1_out, d_ff_1_q);
  Clock clock_1 (.out(clock_1_out));
  not not_2 (not_2_out, d_ff_2_q);
  not not_3 (not_3_out, d_ff_3_q);
  and and_1 (and_1_out, not_1_out, not_2_out, not_3_out);
  and and_2 (and_2_out, d_ff_1_q, not_2_out, not_3_out);
  and and_3 (and_3_out, not_1_out, d_ff_2_q, not_3_out);
  and and_4 (and_4_out, d_ff_1_q, d_ff_2_q, not_3_out);
  and and_5 (and_5_out, not_1_out, not_2_out, d_ff_3_q);
  and and_6 (and_6_out, d_ff_1_q, not_2_out, d_ff_3_q);
  or or_1 (or_1_out, and_1_out, and_3_out, and_5_out);
  or or_2 (or_2_out, and_3_out, and_2_out);
  or or_3 (or_3_out, and_4_out, and_5_out);
  D_Flip_Flop d_ff_1 (.clk(clock_1_out), .D(or_1_out), .Q(d_ff_1_q));  // open: Qn, preset, en, reset
  D_Flip_Flop d_ff_2 (.clk(clock_1_out), .D(or_2_out), .Q(d_ff_2_q));  // open: Qn, preset, en, reset
  D_Flip_Flop d_ff_3 (.clk(clock_1_out), .D(or_3_out), .Q(d_ff_3_q));  // open: Qn, preset, en, reset
  LED S2 (.in(d_ff_3_q));
  LED S1 (.in(d_ff_2_q));
  LED S0 (.in(d_ff_1_q));
  LED led_1 (.in(or_4_out));
  or or_4 (or_4_out, and_1_out, and_4_out, and_5_out, and_6_out);
  LED led_2 (.in(and_3_out));
  LED led_3 (.in(and_2_out));
  LED led_4 (.in(or_5_out));
  or or_5 (or_5_out, and_1_out, and_2_out, and_3_out, and_4_out);
  LED led_5 (.in(and_6_out));
  LED led_6 (.in(and_5_out));

  // Notes on the sheet:
  //   000
  //   100
  //   010
  //   110
  //   001
  //   101
  //   S0*
  //   S1*
  //   S2*
  //   State
  //   A
  //   B
endmodule
